// Logisim project nandcpu.circ as structural Verilog: 5 circuits, main circuit Main
module Rotate_12 (
  input  Clock,
  input  Reset,
  output Pin_0,
  output Pin_1,
  output Pin_2,
  output Pin_3,
  output Pin_4,
  output Pin_5,
  output Pin_6,
  output Pin_7,
  output Pin_8,
  output Pin_9,
  output Pin_10,
  output Pin_11,
  output [3:0] Binary_Out
);

  wire comparator_1_eq, comparator_2_eq, comparator_3_eq, comparator_4_eq, comparator_5_eq, comparator_6_eq,
       comparator_7_eq, comparator_8_eq, comparator_9_eq, comparator_10_eq, comparator_11_eq,
       comparator_12_eq;

  Counter #(.width(4), .max('hb), .trigger("falling")) counter_1 (
    .Q(Binary_Out), .clk(Clock), .clr(Reset));  // open: load, D, count, carry
  Comparator #(.width(4)) comparator_1 (.a(4'b0000), .b(Binary_Out), .eq(comparator_1_eq));  // open: gt, lt
  Comparator #(.width(4)) comparator_2 (.a(4'b0001), .b(Binary_Out), .eq(comparator_2_eq));  // open: gt, lt
  Comparator #(.width(4)) comparator_3 (.a(4'b0010), .b(Binary_Out), .eq(comparator_3_eq));  // open: gt, lt
  Comparator #(.width(4)) comparator_4 (.a(4'b0011), .b(Binary_Out), .eq(comparator_4_eq));  // open: gt, lt
  Comparator #(.width(4)) comparator_5 (.a(4'b0100), .b(Binary_Out), .eq(comparator_5_eq));  // open: gt, lt
  Comparator #(.width(4)) comparator_6 (.a(4'b0101), .b(Binary_Out), .eq(comparator_6_eq));  // open: gt, lt
  Comparator #(.width(4)) comparator_7 (.a(4'b0110), .b(Binary_Out), .eq(comparator_7_eq));  // open: gt, lt
  Comparator #(.width(4)) comparator_8 (.a(4'b0111), .b(Binary_Out), .eq(comparator_8_eq));  // open: gt, lt
  Comparator #(.width(4)) comparator_9 (.a(4'b1000), .b(Binary_Out), .eq(comparator_9_eq));  // open: gt, lt
  Comparator #(.width(4)) comparator_10 (.a(4'b1001), .b(Binary_Out), .eq(comparator_10_eq));  // open: gt, lt
  Comparator #(.width(4)) comparator_11 (.a(4'b1010), .b(Binary_Out), .eq(comparator_11_eq));  // open: gt, lt
  Comparator #(.width(4)) comparator_12 (.a(4'b1011), .b(Binary_Out), .eq(comparator_12_eq));  // open: gt, lt
  and and_1 (Pin_0, Clock, comparator_1_eq);
  and and_2 (Pin_1, Clock, comparator_2_eq);
  and and_3 (Pin_2, Clock, comparator_3_eq);
  and and_4 (Pin_3, Clock, comparator_4_eq);
  and and_5 (Pin_4, Clock, comparator_5_eq);
  and and_6 (Pin_5, Clock, comparator_6_eq);
  and and_7 (Pin_6, Clock, comparator_7_eq);
  and and_8 (Pin_7, Clock, comparator_8_eq);
  and and_9 (Pin_8, Clock, comparator_9_eq);
  and and_10 (Pin_9, Clock, comparator_10_eq);
  and and_11 (Pin_10, Clock, comparator_11_eq);
  and and_12 (Pin_11, Clock, comparator_12_eq);
endmodule

module Main (
);

  wire ALU, bit_extractor_1_out_3, bit_extractor_2_out_3, clock_1_out, comparator_1_eq, Fetch__Op_1,
       Fetch__Op_2, Fetch__Result, Fetch_Op_1, Fetch_Op_2, Fetch_Result, not_1_out, not_2_out, Op_1, Op_2,
       or_1_out, Reset, Store__Op_1, Store__Op_2, Store__Result, Store_Op_1, Store_Op_2, Write_Result;
  wire [3:0] Op_1_Bit, Op_2_Bit, Result_Bit, rotate_12_1_binary_out;
  wire [11:0] multiplexer_1_out, Op_1_Addr, Op_2_Addr, PC, Result_Addr;
  wire [15:0] MemBus, ram_1_data, register_1_q, register_2_q, register_3_q, register_6_q, Result;

  Button button_1 (.out(Reset));
  Register #(.width(16)) register_1 (.D(MemBus), .Q(register_1_q), .clk(Store__Op_1), .clr(Reset));  // open: en
  Register #(.width(16)) register_2 (.D(MemBus), .Q(register_2_q), .clk(Store__Op_2), .clr(Reset));  // open: en
  Register #(.width(16)) register_3 (.D(MemBus), .Q(register_3_q), .clk(Store__Result), .clr(Reset));  // open: en
  Clock clock_1 (.out(clock_1_out));
  Addresssplitter addresssplitter_1 (.Data_In(register_1_q), .Bit_Out(Op_1_Bit), .Address_Out(Op_1_Addr));
  Addresssplitter addresssplitter_2 (.Data_In(register_2_q), .Bit_Out(Op_2_Bit), .Address_Out(Op_2_Addr));
  Addresssplitter addresssplitter_3 (.Data_In(register_3_q), .Bit_Out(Result_Bit), .Address_Out(Result_Addr));
  Rotate_12 rotate_12_1 (
    .Clock(clock_1_out), .Reset(Reset), .Binary_Out(rotate_12_1_binary_out), .Pin_0(Fetch__Op_1),
    .Pin_1(Store__Op_1), .Pin_2(Fetch__Op_2), .Pin_3(Store__Op_2), .Pin_4(Fetch__Result),
    .Pin_5(Store__Result), .Pin_6(Fetch_Op_1), .Pin_7(Store_Op_1), .Pin_8(Fetch_Op_2), .Pin_9(Store_Op_2),
    .Pin_10(Fetch_Result), .Pin_11(Write_Result));
  or or_1 (or_1_out, Fetch__Op_1, Fetch__Op_2, Fetch__Result);
  Bit_Extractor bit_extractor_1 (.Bit_Select(Op_1_Bit), .Data(MemBus), .out_3(bit_extractor_1_out_3));
  Bit_Extractor bit_extractor_2 (.Bit_Select(Op_2_Bit), .Data(MemBus), .out_3(bit_extractor_2_out_3));
  nand nand_1 (ALU, Op_1, Op_2);
  Counter #(.width(12), .max('hfff)) counter_1 (.Q(PC), .clk(or_1_out), .clr(Reset));  // open: load, D, count, carry
  Register #(.width(1)) register_4 (.D(bit_extractor_1_out_3), .Q(Op_1), .clk(Store_Op_1), .clr(Reset));  // open: en
  Register #(.width(1)) register_5 (.D(bit_extractor_2_out_3), .Q(Op_2), .clk(Store_Op_2), .clr(Reset));  // open: en
  Multiplexer #(.select(4), .width(12)) multiplexer_1 (
    .in1(PC), .in2(PC), .in3(PC), .in4(PC), .in5(PC), .in6(PC), .in7(Op_1_Addr), .in8(Op_1_Addr),
    .in9(Op_2_Addr), .in10(Op_2_Addr), .in11(Result_Addr), .in12(Result_Addr), .out(multiplexer_1_out),
    .sel(rotate_12_1_binary_out));  // open: in0, in13, in14, in15
  Comparator #(.width(4), .mode("unsigned")) comparator_1 (
    .a(rotate_12_1_binary_out), .b(4'b1011), .eq(comparator_1_eq));  // open: gt, lt
  Register #(.width(16)) register_6 (.D(MemBus), .Q(register_6_q), .clk(Fetch_Result), .clr(Reset));  // open: en
  RAM #(.addrWidth(12), .dataWidth(16)) ram_1 (
    .addr(multiplexer_1_out), .data(ram_1_data), .clk(Write_Result), .ld(not_1_out));  // open: sel, clr
  not not_1 (not_1_out, comparator_1_eq);
  Bit_Injector bit_injector_1 (.Bit(ALU), .Bit_Select(Result_Bit), .Data(register_6_q), .out_4(Result));
  assign MemBus = not_2_out ? ram_1_data : 16'bz;  // Controlled_Buffer controlled_buffer_1
  not not_2 (not_2_out, comparator_1_eq);
  assign ram_1_data = comparator_1_eq ? Result : 16'bz;  // Controlled_Buffer controlled_buffer_2
endmodule

module Addresssplitter (
  input  [15:0] Data_In,
  output [3:0] Bit_Out,
  output [11:0] Address_Out
);


  assign Address_Out = Data_In[15:4];
  assign Bit_Out = Data_In[3:0];
endmodule

module Bit_Extractor (
  input  [3:0] Bit_Select,
  input  [15:0] Data,
  output out_3
);

  wire [15:0] and_1_out, shifter_1_out;

  Shifter #(.width(16)) shifter_1 (.in(16'h1), .\dist (Bit_Select), .out(shifter_1_out));
  assign and_1_out = shifter_1_out & Data;  // AND_Gate and_1, 16 bits wide
  or or_1 (out_3, and_1_out[0], and_1_out[1], and_1_out[2], and_1_out[3], and_1_out[4], and_1_out[5], and_1_out[6], and_1_out[7], and_1_out[8], and_1_out[9], and_1_out[10], and_1_out[11], and_1_out[12], and_1_out[13], and_1_out[14], and_1_out[15]);
endmodule

module Bit_Injector (
  input  Bit,
  input  [3:0] Bit_Select,
  input  [15:0] Data,
  output [15:0] out_4
);

  wire not_1_out;
  wire [15:0] and_1_out, controlled_buffer_1_out, Mask, not_2_out;

  not not_1 (not_1_out, Bit);
  assign not_2_out = ~Mask;  // NOT_Gate not_2, 16 bits wide
  assign controlled_buffer_1_out = Bit ? Mask : 16'bz;  // Controlled_Buffer controlled_buffer_1
  assign controlled_buffer_1_out = not_1_out ? {16{1'b0}} : 16'bz;  // Controlled_Buffer controlled_buffer_2
  Shifter #(.width(16)) shifter_1 (.in(16'h1), .\dist (Bit_Select), .out(Mask));
  assign and_1_out = not_2_out & Data;  // AND_Gate and_1, 16 bits wide
  assign out_4 = controlled_buffer_1_out | and_1_out;  // OR_Gate or_1, 16 bits wide
endmodule
